# Fritzing sketch Control (saved by Fritzing 0.9.3b)
circuit board: 6.88818cm x 8.67289cm
breadboards: 1

parts:
  Motor_Driver = L293D [package=THT]
  LED1 = LED - 5mm [color="Red (633nm)" package="5 mm [THT]"]
  LED2 = LED - 5mm [color="Red (633nm)" package="5 mm [THT]"]
  LED3 = LED - 5mm [color="Red (633nm)" package="5 mm [THT]"]
  LED4 = LED - 5mm [color="Red (633nm)" package="5 mm [THT]"]
  LED5 = LED - 5mm [color="Red (633nm)" package="5 mm [THT]"]
  LED6 = LED - 5mm [color="Red (633nm)" package="5 mm [THT]"]
  LED7 = LED - 5mm [color="Red (633nm)" package="5 mm [THT]"]
  LED8 = LED - 5mm [color="Red (633nm)" package="5 mm [THT]"]
  LED11 = LED - 5mm [color="Red (633nm)" package="5 mm [THT]"]
  LED12 = LED - 5mm [color="Red (633nm)" package="5 mm [THT]"]
  LED13 = LED - 5mm [color="Red (633nm)" package="5 mm [THT]"]
  LED14 = LED - 5mm [color="Red (633nm)" package="5 mm [THT]"]
  LED15 = LED - 5mm [color="Red (633nm)" package="5 mm [THT]"]
  LED16 = LED - 5mm [color="Red (633nm)" package="5 mm [THT]"]
  LED17 = LED - 5mm [color="Red (633nm)" package="5 mm [THT]"]
  LED18 = LED - 5mm [color="Red (633nm)" package="5 mm [THT]"]
  U2 = LM124-324 Quad Opamp [package="DIP (Dual Inline)"]
  R1 = Trimmer Potentiometer [maximum_resistance=10kΩ package=THT]
  U1 = LM124-324 Quad Opamp [package="DIP (Dual Inline)"]
  Nano = Arduino Nano (Rev3.0)
  R2 = Resistor [tolerance=±5% resistance=220 package=THT]
  R3 = Resistor [tolerance=±5% resistance=220 package=THT]
  R4 = Resistor [tolerance=±5% resistance=220 package=THT]
  R5 = Resistor [tolerance=±5% resistance=220 package=THT]
  R6 = Resistor [tolerance=±5% resistance=220 package=THT]
  R8 = Resistor [tolerance=±5% resistance=220 package=THT]
  R9 = Resistor [tolerance=±5% resistance=220 package=THT]
  R10 = Resistor [tolerance=±5% resistance=220 package=THT]
  R11 = Resistor [tolerance=±5% resistance=220 package=THT]

nets:
  N1: Motor_Driver.Enable_1, Nano.D6
  N2: Motor_Driver.In_1, Nano.D7
  N3: Motor_Driver.0V, R10.Pin_1
  N4: Motor_Driver.In_2, Nano.D8
  N5: Motor_Driver.Enable_2, Nano.D5
  N6: Motor_Driver.In_3, Nano.D4
  N7: Motor_Driver.In_4, Nano.D13/SCK
  N8: Motor_Driver.+V, Nano.5V
  N9: LED1.cathode, LED2.cathode, LED3.cathode, LED4.cathode, LED5.cathode, LED6.cathode, LED7.cathode, LED8.cathode, LED11.anode, LED12.anode, LED13.anode, LED14.anode, LED15.anode, LED16.anode, LED17.anode, LED18.anode, U2.VCC+, R1.leg1, U1.VCC+, Nano.VIN
  N10: LED1.anode, U1.2IN+, R3.Pin_1
  N11: LED2.anode, U1.4IN+, R11.Pin_1
  N12: LED3.anode, U2.4IN+, R5.Pin_0
  N13: LED4.anode, U2.2IN+, R8.Pin_0
  N14: LED5.anode, U2.1IN+, R10.Pin_0
  N15: LED6.anode, U1.3IN+, R4.Pin_0
  N16: LED7.anode, U1.1IN+, R6.Pin_1
  N17: LED8.anode, U2.3IN+, R9.Pin_1
  N18: LED11.cathode, LED12.cathode, LED13.cathode, LED14.cathode, LED15.cathode, LED16.cathode, LED17.cathode, LED18.cathode, Nano.GND, R2.Pin_0, R4.Pin_1, R5.Pin_1, R8.Pin_1, R9.Pin_0, R11.Pin_0
  N19: U2.1OUT, Nano.D1/TX
  N20: U2.1IN-, U2.2IN-, U2.3IN-, U2.4IN-, R1.wiper, U1.1IN-, U1.2IN-, U1.3IN-, U1.4IN-
  N21: U2.2OUT, Nano.D0/RX
  N22: U2.3OUT, Nano.D2
  N23: U2.VCC-, U1.VCC-
  N24: U2.4OUT, Nano.D3
  N25: R1.leg2, R2.Pin_1, R3.Pin_0, R6.Pin_0
  N26: U1.1OUT, Nano.D11/MOSI
  N27: U1.2OUT, Nano.D12/MISO
  N28: U1.3OUT, Nano.D9
  N29: U1.4OUT, Nano.D10
